# Fritzing sketch SecureWatch - Fritzing (saved by Fritzing 0.9.3b)
breadboards: 1

parts:
  U2 = NodeMCU V3.0
  LED1 = LED - 3mm [color="Green (560nm)" package="3 mm [THT]"]
  LED2 = LED - 3mm [color="Yellow (592nm)" package="3 mm [THT]"]
  R1 = Resistor [tolerance=±5% resistance=220 package="0805 [SMD]"]
  R2 = Resistor [tolerance=±5% resistance=220 package="0805 [SMD]"]
  S1 = Pushbutton [package="[THT]"]

nets:
  N1: U2.3V3, S1.Pin_3, S1.Pin_4
  N2: U2.GND, R1.Pin_1, R2.Pin_0
  N3: U2.D5, LED1.anode
  N4: U2.D6, LED2.anode
  N5: U2.D8, R2.Pin_1, S1.Pin_1, S1.Pin_2
  N6: LED1.cathode, LED2.cathode, R1.Pin_0

custom parts:
  NodeMCU V3.0: NodeMcu V3 Lua WIFI Development Board
